// Logisim project CPU.circ as structural Verilog
module halfadder (
  input  A,
  input  B,
  output SUM,
  output CARRY
);

  xor xor_1 (SUM, A, B);
  and and_1 (CARRY, A, B);
endmodule

module fulladder (
  input  CIN,
  input  A,
  input  B,
  output Sum,
  output Carry
);

  wire and_1_out, and_2_out, xor_1_out;

  xor xor_1 (xor_1_out, A, B);
  and and_1 (and_1_out, A, B);
  xor xor_2 (Sum, xor_1_out, CIN);
  and and_2 (and_2_out, CIN, xor_1_out);
  or or_1 (Carry, and_2_out, and_1_out);
endmodule

module fourbitadder (
  input  in_1,
  input  A1,
  input  A3,
  input  B1,
  input  B3,
  input  A2,
  input  A4,
  input  B2,
  input  B4,
  output out_10,
  output out_11,
  output out_12,
  output out_13,
  output out_14
);

  wire fulladder_1_carry, fulladder_2_carry, fulladder_3_carry;

  fulladder fulladder_1 (.CIN(in_1), .A(A1), .B(A3), .Sum(out_10), .Carry(fulladder_1_carry));
  fulladder fulladder_2 (.CIN(fulladder_1_carry), .A(B1), .B(B3), .Sum(out_11), .Carry(fulladder_2_carry));
  fulladder fulladder_3 (.CIN(fulladder_2_carry), .A(A2), .B(A4), .Sum(out_12), .Carry(fulladder_3_carry));
  fulladder fulladder_4 (.CIN(fulladder_3_carry), .A(B2), .B(B4), .Sum(out_13), .Carry(out_14));
endmodule
